// Logisim project LC-3.circ as structural Verilog: 18 circuits, main circuit main
module main (
  input  Reset,
  output out_2,
  output out_3,
  output out_4,
  output out_5,
  output out_6,
  output out_7,
  output out_8,
  output [15:0] out_9,
  output [15:0] out_10,
  output [15:0] out_11,
  output [15:0] out_12,
  output [15:0] out_13,
  output [15:0] out_14,
  output [15:0] out_15,
  output [15:0] out_16,
  output [15:0] out_17,
  output halt,
  output [15:0] out_19,
  output [15:0] out_20,
  output [15:0] out_21,
  output [15:0] out_22
);

  wire Arith, decodeir_1_writereg, getcst_1_usecst, or16_1_out_2, or16_2_out_2, ramctrl_1_memload,
       ramctrl_1_memstore;
  wire [1:0] _2mem;
  wire [2:0] nzp_2_nzp, SR;
  wire [15:0] AluOUT, getcst_1_cst, LDI_STI, load_store_1_regin, registres_1_out_sr1, registres_1_out_sr2;

  BiClock biclock_1 (.reset(Reset), .signal0(out_2), .signal1(out_3));
  RegPC regpc_1 (
    .H(out_3), .PC(out_9), .Reset(Reset), .IR(out_10), .R(registres_1_out_sr1), .TestNZP(out_5), .Jump(out_4));
  // Probe on out_9
  // Probe on out_11
  GetAddr getaddr_1 (
    .PC(out_9), .R(registres_1_out_sr1), .IR(out_10), .Addr(out_11), .Fetch(out_2), .Exec(out_3),
    ._2mem(_2mem), .LDI_STI(LDI_STI));
  // Probe on out_12
  LED led_1 (.in(out_6));
  RamCtrl ramctrl_1 (
    .Store(out_7), .Exec(out_3), .Load(out_6), .MemStore(ramctrl_1_memstore), .MemLoad(ramctrl_1_memload),
    ._2mem(_2mem), .Fetch(out_2));
  LED led_2 (.in(out_7));
  // Probe on out_13
  RAM #(.addrWidth(16), .dataWidth(16), .bus("separate")) ram_1 (
    .addr(out_11), .din(out_12), .data(out_13), .str(ramctrl_1_memstore), .clk(ramctrl_1_memstore),
    .ld(ramctrl_1_memload));  // open: sel, clr
  Register #(.width(16), .trigger("falling")) RegIR (.D(out_13), .Q(out_10), .clk(out_2));  // open: en, clr
  DecodeIR decodeir_1 (
    .IR(out_10), .WriteReg(decodeir_1_writereg), .Arith(Arith), .Load(out_6), .Store(out_7), .Jump(out_4),
    ._2mem(_2mem));
  Load_Store load_store_1 (
    .JumpInstr(out_4), .IR(out_10), .Addr(out_11), .MemOUT(out_13), .RegIn(load_store_1_regin),
    .Arith(Arith), .AluOUT(AluOUT));
  // Probe on SR
  // Probe on out_10[8:6]
  // Probe on out_10[2:0]
  // Probe on getcst_1_cst
  GetCst getcst_1 (.IR(out_10), .Cst(getcst_1_cst), .UseCst(getcst_1_usecst));
  // Probe on out_10[15:14]
  and and_1 (out_8, decodeir_1_writereg, out_3);
  Registres registres_1 (
    .SR1(out_10[8:6]), .IN(load_store_1_regin), .SR2(out_10[2:0]), .WriteReg(out_8), .DR_SR(SR),
    .OUT_SR1(registres_1_out_sr1), .OUT_SR2(registres_1_out_sr2), .OUT_SR(out_12), .R0(out_14), .R1(out_15),
    .R2(out_16), .R3(out_17), .R4(out_19), .R5(out_20), .R6(out_21), .R7(out_22));
  // Probe on registres_1_out_sr1
  ALU alu_1 (
    ._4(out_10[4]), .Input1(registres_1_out_sr1), .Input2(registres_1_out_sr2), .Cst(getcst_1_cst),
    .UseCst(getcst_1_usecst), .e2(out_10[15:14]), .Output(AluOUT));
  // Probe on registres_1_out_sr2
  // Probe on AluOUT
  // Probe on nzp_2_nzp
  NZP nzp_2 (.RES(load_store_1_regin), .IR(out_10), .TestNZP(out_5), .WriteReg(out_8), .NZP(nzp_2_nzp));
  Or16 or16_1 (.in_1(out_10), .out_2(or16_1_out_2));
  Or16 or16_2 (.in_1(out_9), .out_2(or16_2_out_2));
  // Probe on out_14
  // Probe on out_15
  // Probe on out_16
  // Probe on out_17
  // Probe on out_19
  // Probe on out_20
  // Probe on out_21
  // Probe on out_22
  and and_2 (halt, ~or16_1_out_2, or16_2_out_2);  // AND_Gate
  JSR_JSRR jsr_jsrr_1 (.DR(out_10[11:9]), .JumpInstr(out_4), .SR(SR));
  LDI_STI ldi_sti_1 (.MemOUT(out_13), .Exec(out_3), .LDI_STI(LDI_STI));

  // Other names for the same wires on the sheet: Addr[15:0] = out_11; Condition = out_5; Exec = out_3; Fetch = out_2;
  //   IR[15:0] = out_10; DR[2:0] = out_10[11:9]; JumpInstr = out_4; Load = out_6; MemIN[15:0] = out_12;
  //   MemOUT[15:0] = out_13; PC[15:0] = out_9; R0[15:0] = out_14; R1[15:0] = out_15; R2[15:0] = out_16;
  //   R3[15:0] = out_17; R4[15:0] = out_19; R5[15:0] = out_20; R6[15:0] = out_21; R7[15:0] = out_22; Store = out_7;
  //   WriteReg = out_8

  // Notes on the sheet:
  //   R
  //   IR
  //   R
  //   IR
  //   RAM
  //   GetRegs
  //   Traces (NE PAS MODIFIER)______________________________________________________________________________________________________
  //   GetOp
  //   Arret des traces au 1er NOP
endmodule

module ALU (
  input  _4,
  input  [15:0] Input1,
  input  [15:0] Input2,
  input  [15:0] Cst,
  input  UseCst,
  input  [1:0] e2,
  output [15:0] Output
);

  wire [15:0] adder_1_out, and_1_out, multiplexer_1_out, not_1_out, set_reset_1_output;

  Multiplexer #(.width(16), .enable("false")) multiplexer_1 (
    .in0(Input2), .in1(Cst), .out(multiplexer_1_out), .sel(UseCst));
  Adder #(.width(16)) adder_1 (.a(multiplexer_1_out), .b(Input1), .out(adder_1_out));  // open: cin, cout
  assign and_1_out = Input1 & multiplexer_1_out;  // AND_Gate and_1, 16 bits wide
  Multiplexer #(.select(2), .width(16), .enable("false")) multiplexer_2 (
    .in0(adder_1_out), .in1(and_1_out), .in2(not_1_out), .in3(set_reset_1_output), .out(Output), .sel(e2));
  assign not_1_out = ~Input1;  // NOT_Gate not_1, 16 bits wide
  Set_Reset set_reset_1 (.Input2(multiplexer_1_out), .Input1(Input1), ._4(_4), .Output(set_reset_1_output));

  // Notes on the sheet:
  //   01 : ET 
  //   00 : ADD
  //   10 : NOT 
  //   11:SET/RESET
  //   Bit swap
endmodule

module BiClock (
  input  reset,
  output signal0,
  output signal1
);

  wire and_1_out, horloge_out, not_1_out, register_1_q;

  Clock horloge (.out(horloge_out));
  not not_1 (not_1_out, register_1_q);
  Register #(.width(1), .trigger("falling")) register_1 (
    .D(not_1_out), .Q(register_1_q), .clk(horloge_out), .clr(reset));  // open: en
  and and_1 (and_1_out, horloge_out, ~reset);  // AND_Gate
  and and_2 (signal0, ~register_1_q, and_1_out);  // AND_Gate
  and and_3 (signal1, register_1_q, and_1_out);

  // Notes on the sheet:
  //   Ce module divise une horloge en deux sous-horloges alternées
  //   Chronogrammes :
  //   horloge: 0101010101 signal0: 0100010001 signal1: 000100010
  //   registre 1-bit
  //   Enable
  //   select : 0 / 1
endmodule

module DecodeIR (
  input  [15:0] IR,
  output Jump,
  output Arith,
  output WriteReg,
  output Load,
  output Store,
  output [1:0] _2mem
);

  wire and_1_out, multiplexer_1_out, multiplexer_2_out;

  Demultiplexer #(.select(2), .enable("false")) demultiplexer_1 (
    .out0(Jump), .out1(Arith), .out2(Load), .out3(Store), .in(1'b1), .sel(IR[13:12]));
  Multiplexer #(.select(2), .enable("false")) multiplexer_1 (
    .in0(1'b0), .in1(1'b1), .in2(1'b0), .in3(1'b0), .out(multiplexer_1_out), .sel(IR[15:14]));
  Multiplexer #(.select(2), .enable("false")) multiplexer_2 (
    .in0(1'b0), .in1(1'b0), .in2(1'b1), .in3(1'b0), .out(multiplexer_2_out), .sel(IR[15:14]));
  and and_1 (and_1_out, multiplexer_1_out, Jump);
  and and_2 (_2mem[0], Load, multiplexer_2_out);
  and and_3 (_2mem[1], Store, multiplexer_2_out);
  or or_1 (WriteReg, and_1_out, Arith, Load);

  // Notes on the sheet:
  //   constante 0
  //   constante 0
  //   constante 1
  //   14 et 15ième bit
  //   constante 1
  //    pour JSR/JSRR : 01
  //   constante 1
  //   13-12 type d'instruction
  //   00 : saut
  //   01 : arith
  //   10 : load
  //   11 : store
  //   14 et 15ième bit
  //    pour LDI/STI : 10
  //   si LDI ou STI vaut 1
  //   0 sinon
  //    pour JSR/JSRR : 01 pas unique instruction à 01
  //   si les deux alors JSR/JSRR
  //   1 si Store donc STI, 0 sinon
  //   1 si Load donc LDI, 0 sinon
  //   01 : LDI
  //   10 : STI
endmodule

module GetAddr (
  input  [15:0] IR,
  input  [15:0] R,
  input  Fetch,
  input  [15:0] LDI_STI,
  input  [15:0] PC,
  input  Exec,
  input  [1:0] _2mem,
  output [15:0] Addr
);

  wire and_1_out, or_1_out;
  wire [15:0] adder_1_out, adder_2_out, multiplexer_1_out, multiplexer_2_out, multiplexer_3_out,
       multiplexer_4_out, offset6_1_off6, offset9_1_off9, subtractor_1_out, subtractor_2_out;

  Offset9 offset9_1 (.IR(IR), .Off9(offset9_1_off9));
  Offset6 offset6_1 (.IR(IR), .Off6(offset6_1_off6));
  Adder #(.width(16)) adder_1 (.a(offset6_1_off6), .b(R), .out(adder_1_out));  // open: cin, cout
  Adder #(.width(16)) adder_2 (.a({16{1'b0}}), .b(offset9_1_off9), .out(adder_2_out), .cin(1'b1));  // open: cout
  or or_1 (or_1_out, _2mem[1], _2mem[0]);
  Subtractor #(.width(16)) subtractor_1 (.a(adder_1_out), .b(PC), .out(subtractor_1_out));  // open: bin, bout
  Subtractor #(.width(16)) subtractor_2 (.a(LDI_STI), .b(PC), .out(subtractor_2_out));  // open: bin, bout
  Multiplexer #(.select(2), .width(16), .enable("false")) multiplexer_1 (
    .in0(adder_2_out), .in1(subtractor_1_out), .in2(adder_2_out), .in3(adder_2_out), .out(multiplexer_1_out),
    .sel(IR[15:14]));
  and and_1 (and_1_out, Exec, or_1_out);
  Multiplexer #(.width(16), .enable("false")) multiplexer_2 (
    .in0(multiplexer_4_out), .in1(subtractor_2_out), .out(multiplexer_2_out), .sel(and_1_out));
  Multiplexer #(.select(2), .width(16), .enable("false")) multiplexer_3 (
    .in0({16{1'b0}}), .in1({16{1'b0}}), .in2(multiplexer_1_out), .in3(multiplexer_1_out),
    .out(multiplexer_3_out), .sel(IR[13:12]));
  Multiplexer #(.width(16), .enable("false")) multiplexer_4 (
    .in0(multiplexer_3_out), .in1({16{1'b0}}), .out(multiplexer_4_out), .sel(Fetch));
  Adder #(.width(16)) adder_3 (.a(multiplexer_2_out), .b(PC), .out(Addr));  // open: cin, cout

  // Notes on the sheet:
  //   constante 0
  //   pc +1 en général
  //   offset9
  //   offset6
  //   constante 1
  //   pc+offset9
  //   offset6 +R
  //   offset6 +R - PC
  //   LDI/STI pas besoin du PC
  //    quand calcul de la 2ieme adresse
  //   execution et (sti ou ldi)
  //   pas un offset de 9
  //   mais 6 pour 01
  //   00 : ld/st/br
  //   01 : ldr/str
  //   10 : ldi/sti
  //   11 : lea/jump
  //   car baseR pas de pc
  //   rajouté à la fin donc pour égaliser
  //   LDI/STI ou autre ?
  //   constante 0
  //   plus tard 0+pc
  //   00 : jmp
  //   01 : arith
  //   10 : load
  //   11 : store
  //   offset+PC
  //   constante 0
  //   plus tard 0+pc
  //   calcul d'adresse
  //    à fetch uniquement
  //   Adresse Memoire
endmodule

module GetCst (
  input  [15:0] IR,
  output [15:0] Cst,
  output UseCst
);

  assign Cst = {{11{IR[4]}}, IR[4:0]};  // Bit_Extender bit_extender_1

  assign UseCst = IR[5];
endmodule

module JSR_JSRR (
  input  [2:0] DR,
  input  JumpInstr,
  output [2:0] SR
);

  Multiplexer #(.width(3), .enable("false")) multiplexer_1 (.in0(DR), .in1(3'b111), .out(SR), .sel(JumpInstr));

  // Notes on the sheet:
  //   R7
  //   Si JSR ou JSSR alors R7
endmodule

module Load_Store (
  input  JumpInstr,
  input  [15:0] IR,
  input  [15:0] MemOUT,
  input  [15:0] Addr,
  input  [15:0] AluOUT,
  input  Arith,
  output [15:0] RegIn
);

  wire [15:0] adder_1_out, multiplexer_1_out, multiplexer_2_out;

  Multiplexer #(.select(2), .width(16), .enable("false")) multiplexer_1 (
    .in0(MemOUT), .in1(MemOUT), .in2(MemOUT), .in3(Addr), .out(multiplexer_1_out), .sel(IR[15:14]));
  Multiplexer #(.width(16), .enable("false")) multiplexer_2 (
    .in0(multiplexer_1_out), .in1(adder_1_out), .out(multiplexer_2_out), .sel(JumpInstr));
  Adder #(.width(16)) adder_1 (.a(Addr), .b({16{1'b0}}), .out(adder_1_out), .cin(1'b1));  // open: cout
  Multiplexer #(.width(16), .enable("false")) multiplexer_3 (
    .in0(multiplexer_2_out), .in1(AluOUT), .out(RegIn), .sel(Arith));

  // Notes on the sheet:
  //   Connaitre l'instruction
  //   00 : ld/st
  //   01 : ldr/str
  //   10 : ldi/sti
  //   11 : lea
  //   constante 0
  //   savoir si l'on fait un JSR/JSRR ou non 
  //   load/store
  //   Si arithmétique alors juste sortie
  //   JSR/JSRR
  //   l'additionneur sert pour laisser passer une valeur par défaut dans le circuit quand ce n'est pas JSR/JSRR
endmodule

module LDI_STI (
  input  [15:0] MemOUT,
  input  Exec,
  output [15:0] LDI_STI
);

  Register #(.width(16)) register_1 (.D(MemOUT), .Q(LDI_STI), .clk(Exec));  // open: en, clr

  // Notes on the sheet:
  //   le deuxième appel mémoire 
  //   Quand au est au temps exec1 informé le circuit getAddr pour effectuer
endmodule

module NZP (
  input  [15:0] RES,
  input  WriteReg,
  input  [15:0] IR,
  output TestNZP,
  output [2:0] NZP
);

  wire [2:0] and_1_out, comparator_1_lt, multiplexer_1_out;

  Comparator #(.width(16)) comparator_1 (
    .a({16{1'b0}}), .b(RES), .gt(comparator_1_lt[2]), .eq(comparator_1_lt[1]), .lt(comparator_1_lt[0]));
  Multiplexer #(.width(3), .enable("false")) multiplexer_1 (
    .in0(multiplexer_1_out), .in1(comparator_1_lt), .out(multiplexer_1_out), .sel(WriteReg));
  assign and_1_out = multiplexer_1_out & IR[11:9];  // AND_Gate and_1, 3 bits wide
  or or_1 (TestNZP, and_1_out[0], and_1_out[1], and_1_out[2]);

  assign NZP = IR[11:9];

  // Notes on the sheet:
  //   constante 0
  //   (Resultat du calcul courant)
  //   (Instruction mettant à jour NZP)
  //   (Instruction courante)
  //   sert pour br
  //   on garde l'ancien
  //   Valeur actuel du registre d'état NZP
  //   si l'un des 3 oui
  //   Test de saut
endmodule

// Off6
module Offset6 (
  input  [15:0] IR,
  output [15:0] Off6
);

  assign Off6 = {{10{IR[5]}}, IR[5:0]};  // Bit_Extender bit_extender_1
endmodule

// Off9
module Offset9 (
  input  [15:0] IR,
  output [15:0] Off9
);

  assign Off9 = {{7{IR[8]}}, IR[8:0]};  // Bit_Extender bit_extender_1
endmodule

// Off11
module Offset11 (
  input  [15:0] IR,
  output [15:0] Off11
);

  assign Off11 = {{5{IR[10]}}, IR[10:0]};  // Bit_Extender bit_extender_1
endmodule

module Or16 (
  input  [15:0] in_1,
  output out_2
);

  wire [3:0] or_1_out;

  assign or_1_out = in_1[3:0] | in_1[7:4] | in_1[11:8] | in_1[15:12];  // OR_Gate or_1, 4 bits wide
  or or_2 (out_2, or_1_out[0], or_1_out[1], or_1_out[2], or_1_out[3]);
endmodule

module RamCtrl (
  input  Load,
  input  Fetch,
  input  Exec,
  input  Store,
  input  [1:0] _2mem,
  output MemLoad,
  output MemStore
);

  wire and_1_out, and_2_out, nor_1_out;

  and and_1 (and_1_out, Load, Exec);
  and and_2 (and_2_out, Exec, Store);
  nor nor_1 (nor_1_out, Fetch, Exec);
  Multiplexer #(.enable("false")) multiplexer_1 (.in0(and_2_out), .in1(nor_1_out), .out(MemStore), .sel(_2mem[1]));
  or or_1 (MemLoad, and_1_out, Fetch, _2mem[1], _2mem[0]);

  // Notes on the sheet:
  //   01 : LDI
  //   10 : STI
  //   1 STI
  //   1 LDI
  //   STI
endmodule

module Registres (
  input  [2:0] SR1,
  input  [15:0] IN,
  input  [2:0] SR2,
  input  WriteReg,
  input  [2:0] DR_SR,
  output [15:0] R0,
  output [15:0] OUT_SR1,
  output [15:0] R1,
  output [15:0] R2,
  output [15:0] R3,
  output [15:0] OUT_SR2,
  output [15:0] R4,
  output [15:0] R5,
  output [15:0] OUT_SR,
  output [15:0] R6,
  output [15:0] R7
);

  wire decoder_1_out0, decoder_1_out1, decoder_1_out2, decoder_1_out3, decoder_1_out4, decoder_1_out5,
       decoder_1_out6, decoder_1_out7;

  Decoder #(.select(3), .disabled(0)) decoder_1 (
    .out0(decoder_1_out0), .out1(decoder_1_out1), .out2(decoder_1_out2), .out3(decoder_1_out3),
    .out4(decoder_1_out4), .out5(decoder_1_out5), .out6(decoder_1_out6), .out7(decoder_1_out7), .sel(DR_SR),
    .en(WriteReg));
  Register #(.width(16), .trigger("falling")) u_R0 (.D(IN), .Q(R0), .clk(decoder_1_out0));  // open: en, clr
  Register #(.width(16), .trigger("falling")) u_R1 (.D(IN), .Q(R1), .clk(decoder_1_out1));  // open: en, clr
  Register #(.width(16), .trigger("falling")) u_R2 (.D(IN), .Q(R2), .clk(decoder_1_out2));  // open: en, clr
  Register #(.width(16), .trigger("falling")) u_R3 (.D(IN), .Q(R3), .clk(decoder_1_out3));  // open: en, clr
  Register #(.width(16), .trigger("falling")) u_R4 (.D(IN), .Q(R4), .clk(decoder_1_out4));  // open: en, clr
  Register #(.width(16), .trigger("falling")) u_R5 (.D(IN), .Q(R5), .clk(decoder_1_out5));  // open: en, clr
  Register #(.width(16), .trigger("falling")) u_R6 (.D(IN), .Q(R6), .clk(decoder_1_out6));  // open: en, clr
  Register #(.width(16), .trigger("falling")) u_R7 (.D(IN), .Q(R7), .clk(decoder_1_out7));  // open: en, clr
  Multiplexer #(.select(3), .width(16), .enable("false")) multiplexer_1 (
    .in0(R0), .in1(R1), .in2(R2), .in3(R3), .in4(R4), .in5(R5), .in6(R6), .in7(R7), .out(OUT_SR1), .sel(SR1));
  Multiplexer #(.select(3), .width(16), .enable("false")) multiplexer_2 (
    .in0(R0), .in1(R1), .in2(R2), .in3(R3), .in4(R4), .in5(R5), .in6(R6), .in7(R7), .out(OUT_SR2), .sel(SR2));
  Multiplexer #(.select(3), .width(16), .enable("false")) multiplexer_3 (
    .in0(R0), .in1(R1), .in2(R2), .in3(R3), .in4(R4), .in5(R5), .in6(R6), .in7(R7), .out(OUT_SR), .sel(DR_SR));
endmodule

module RegPC (
  input  Jump,
  input  H,
  input  Reset,
  input  TestNZP,
  input  [15:0] R,
  input  [15:0] IR,
  output [15:0] PC
);

  wire [15:0] adder_1_out, multiplexer_1_out, multiplexer_2_out, multiplexer_3_out, multiplexer_4_out,
       offset9_1_off9, offset11_1_off11, subtractor_1_out;

  Multiplexer #(.width(16), .enable("false")) multiplexer_1 (
    .in0({16{1'b0}}), .in1(offset9_1_off9), .out(multiplexer_1_out), .sel(TestNZP));
  Offset9 offset9_1 (.IR(IR), .Off9(offset9_1_off9));
  Multiplexer #(.width(16), .enable("false")) multiplexer_2 (
    .in0({16{1'b0}}), .in1(multiplexer_3_out), .out(multiplexer_2_out), .sel(Jump));
  Multiplexer #(.select(2), .width(16), .enable("false")) multiplexer_3 (
    .in0(multiplexer_1_out), .in1(multiplexer_4_out), .in2({16{1'b0}}), .in3(subtractor_1_out),
    .out(multiplexer_3_out), .sel(IR[15:14]));
  Multiplexer #(.width(16), .enable("false")) multiplexer_4 (
    .in0(subtractor_1_out), .in1(offset11_1_off11), .out(multiplexer_4_out), .sel(IR[11]));
  Offset11 offset11_1 (.IR(IR), .Off11(offset11_1_off11));
  Adder #(.width(16)) adder_1 (.a(PC), .b(multiplexer_2_out), .out(adder_1_out), .cin(1'b1));  // open: cout
  Subtractor #(.width(16)) subtractor_1 (.a(R), .b(PC), .out(subtractor_1_out), .bin(1'b1));  // open: bout
  Register #(.width(16), .trigger("falling")) u_PC (.D(adder_1_out), .Q(PC), .clk(H), .clr(Reset));  // open: en

  // Notes on the sheet:
  //   constante 0
  //   00 : BR
  //   01 :JSR/JSSR
  //   10 : (RTI)
  //   11 : JMP
  //   Si nzp = 0
  //   pas BR
  //   constante 0
  //   offset9
  //   1 ou 0
  //   JSR ou JSRR ?
  //   constante 0
  //   JSRR
  //   JSR
  //   offset11
  //   constante 1
  //   constante 1
  //   R-PC
  //   PC <- PC + 1
endmodule

module Set_Reset (
  input  _4,
  input  [15:0] Input2,
  input  [15:0] Input1,
  output [15:0] Output
);

  wire comparator_1_eq, comparator_1_gt, not_1_out;
  wire [3:0] bit_extender_1_out, Sortie, subtractor_1_out;
  wire [15:0] bit_extender_2_out, multiplexer_1_out, shifter_1_out, shifter_2_out, shifter_3_out,
       shifter_4_out;

  Subtractor #(.width(4)) subtractor_1 (.a(4'b1111), .b(Sortie), .out(subtractor_1_out));  // open: bin, bout
  Shifter #(.width(16), .shift("lr")) shifter_1 (.in(Input1), .\dist (Input2[3:0]), .out(shifter_1_out));
  Shifter #(.width(16)) shifter_2 (.in(Input1), .\dist (subtractor_1_out), .out(shifter_2_out));
  Shifter #(.width(16), .shift("lr")) shifter_3 (.in(shifter_2_out), .\dist (subtractor_1_out), .out(shifter_3_out));
  Shifter #(.width(16)) shifter_4 (.in({shifter_1_out[15:1], _4}), .\dist (Input2[3:0]), .out(shifter_4_out));
  Comparator #(.width(4)) comparator_1 (
    .a(Input2[3:0]), .b(4'b0000), .gt(comparator_1_gt), .eq(comparator_1_eq));  // open: lt
  assign bit_extender_1_out = {{3{1'b0}}, comparator_1_gt};  // Bit_Extender bit_extender_1
  not not_1 (not_1_out, comparator_1_eq);
  Subtractor #(.width(4)) subtractor_2 (.a(Input2[3:0]), .b(bit_extender_1_out), .out(Sortie));  // open: bin, bout
  assign bit_extender_2_out = {{15{1'b0}}, not_1_out};  // Bit_Extender bit_extender_2
  Multiplexer #(.width(16), .enable("false")) multiplexer_1 (
    .in0(shifter_3_out), .in1(bit_extender_2_out), .out(multiplexer_1_out), .sel(comparator_1_eq));
  Adder #(.width(16)) adder_1 (.a(shifter_4_out), .b(multiplexer_1_out), .out(Output));  // open: cin, cout

  // Notes on the sheet:
  //   * : on decale vers la gauche pour récupérer uniquement
  //   le n dernier bit que l'on ajoutera au résultat intermédiare
  //   Decalage de n bits
  //   pour avoir le bit à
  //   modifier en derniere
  //   position
  //   *
  //   Bit swap
  //   de 15-n
  //   Decalage de n bits dans l'autre sens
  //   constante 0
  //   décalage
  //   Pb, il manque la fin du mot...
  //   On ajoute la fin du mot si necessaire
  //   décalage de -1
  //   Si le
  //   décalage
  //   vaut 0
  //   alors on
  //   ajoute rien
endmodule
